# Fritzing sketch MPVZ5010_serial (saved by Fritzing 0.9.3b)
breadboards: 1

parts:
  U1 = attiny85 [package=dip]
  R1 = Resistor [tolerance=±5% resistance=220 package="1206 [SMD]"]
  LED1 = LED - 5mm [color="Red (633nm)" package="5 mm [THT]"]
  MPX1 = MPX2010 pressure sensor [part_number=MPX]

nets:
  N1: U1.Pin_3, MPX1.V_out_+
  N2: U1.Pin_4, LED1.anode, MPX1.Vs
  N3: U1.Pin_6, R1.Pin_0
  N4: U1.Pin_8, MPX1.V_out_-
  N5: R1.Pin_1, LED1.cathode

notes:
  Loose cables = USB to TTL
  red = 5V
  brown = GND
  orange = RXD
  green = TXD
  Sensor pins
  - 1 NA
  - 2 Vs
  - 3 GND
  - 4 Vout
  MPVZ5010
  MPVZ5010 Sensor pins
  - 1 NA
  - 2 Vs
  - 3 GND
  - 4 Vout
