# Fritzing sketch MPX5010_battery (saved by Fritzing 0.9.3b)
breadboards: 1

parts:
  MPX1 = MPX2010 pressure sensor [part_number=MPX]
  U1 = attiny85 [package=dip]
  LED1 = LED - 5mm [color="Red (633nm)" package="5 mm [THT]"]
  R1 = Resistor [tolerance=±5% resistance=220 package="0805 [SMD]"]
  BAT1 = Battery Holders [package=battcon_12mm]

nets:
  N1: MPX1.GND, U1.Pin_2
  N2: MPX1.V_out_-, U1.Pin_4, LED1.cathode, BAT1.-
  N3: MPX1.Vs, U1.Pin_8, BAT1.+
  N4: U1.Pin_6, R1.Pin_0
  N5: LED1.anode, R1.Pin_1

notes:
  Using the MPX5010 not 2010
  Using MPX5010 pins are:
  1> Vout
  2> GND
  3>Vs
